// Logisim project circuitoMIPS.circ as structural Verilog: 5 circuits, main circuit main
module main (
  input  in_1
);

  wire ALUSrc, and_1_out, Branch, ClockMain, Jump, MemRead, MemToReg, MemWrite, not_1_out, or_1_out, RegDist,
       RegWrite, ula_1_igual;
  wire [1:0] ALUOp;
  wire [2:0] Cont__ULA_ulactrl, multiplexer_1_out, opcode, rs, rt;
  wire [2:2] rd;
  wire [7:0] adder_1_out, address_Imm, Banco_de_reg_read_data_1, contRT, multiplexer_2_out,
       multiplexer_3_out, multiplexer_4_out, PC_q, ram_1_data, ula_1_r;

  Clock clock_1 (.out(ClockMain));
  Register PC (.D(multiplexer_3_out), .Q(PC_q), .clk(ClockMain), .clr(in_1));  // open: en
  Adder adder_1 (.a(8'h1), .b(PC_q), .out(adder_1_out));  // open: cin, cout
  ROM #(.dataWidth(18)) rom_1 (.addr(PC_q), .data({opcode, rs, rt, rd[2], address_Imm}));  // open: sel
  Multiplexer #(.width(3), .enable("false")) multiplexer_1 (
    .in0(rt), .in1({rd[2], address_Imm[7:6]}), .out(multiplexer_1_out), .sel(RegDist));
  Banco_de_Registradores Banco_de_reg (
    .Read_register_1(rs), .Read_register_2(rt), .Write_data(multiplexer_4_out),
    .Write_register(multiplexer_1_out), .RegWrite(RegWrite), .CLOCK(ClockMain), .CLEAR(in_1),
    .Read_data_1(Banco_de_reg_read_data_1), .Read_data_2(contRT));
  Controle_ULA Cont__ULA (.funct(address_Imm[2:0]), .ALUOp(ALUOp), .ULACtrl(Cont__ULA_ulactrl));
  Unidade_de_Controle unidade_de_controle_1 (
    .opcode(opcode), .RegDst(RegDist), .RegWrite(RegWrite), .ALUSrc(ALUSrc), .MemWrite(MemWrite),
    .MemRead(MemRead), .MemToReg(MemToReg), .Branch(Branch), .Jump(Jump), .out_10(ALUOp));
  Multiplexer #(.width(8), .enable("false")) multiplexer_2 (
    .in0(contRT), .in1(address_Imm), .out(multiplexer_2_out), .sel(ALUSrc));
  ULA ula_1 (
    .A(Banco_de_reg_read_data_1), .B(multiplexer_2_out), .\Função (Cont__ULA_ulactrl),
    .Shamt(address_Imm[5:3]), .R(ula_1_r), .Igual(ula_1_igual));
  not not_1 (not_1_out, ClockMain);
  and and_1 (and_1_out, Branch, ula_1_igual);
  RAM #(.bus("separate")) ram_1 (
    .addr(ula_1_r), .din(contRT), .data(ram_1_data), .str(MemWrite), .clk(not_1_out), .ld(MemRead), .clr(in_1));  // open: sel
  Multiplexer #(.width(8), .enable("false")) multiplexer_3 (
    .in0(adder_1_out), .in1(address_Imm), .out(multiplexer_3_out), .sel(or_1_out));
  or or_1 (or_1_out, Jump, and_1_out);
  Multiplexer #(.width(8), .enable("false")) multiplexer_4 (
    .in0(ram_1_data), .in1(ula_1_r), .out(multiplexer_4_out), .sel(MemToReg));

  // Other names for the same wires on the sheet: ClearMain = in_1; funct[2:0] = address_Imm[2:0];
  //   rd[1:0] = address_Imm[7:6]; shamt[2:0] = address_Imm[5:3]

  // Notes on the sheet:
  //   contents of rom_1 (hex, n*v repeats v):
  //   20601 2080a 20a01 11400 2780 680 cc0 1a40 4b01 1c00b 38003 3800b 4*0 2
endmodule

module Controle_ULA (
  input  [2:0] funct,
  input  [1:0] ALUOp,
  output [2:0] ULACtrl
);

  Multiplexer #(.select(2), .width(3), .enable("false")) multiplexer_1 (
    .in0(3'b000), .in1(3'b101), .in2(funct), .in3(3'b000), .out(ULACtrl), .sel(ALUOp));

  // Notes on the sheet:
  //   Controle ULA
  //   Controle ULA
endmodule

// UC
module Unidade_de_Controle (
  input  [2:0] opcode,
  output RegDst,
  output RegWrite,
  output ALUSrc,
  output MemWrite,
  output MemRead,
  output MemToReg,
  output Branch,
  output Jump,
  output [1:0] out_10
);

  wire and_1_out, and_4_out, and_5_out, and_8_out, and_9_out, nor_2_out;

  nor nor_1 (RegDst, opcode[0], opcode[1], opcode[2]);
  nor nor_2 (nor_2_out, opcode[1], opcode[2]);
  and and_1 (and_1_out, ~opcode[0], ~opcode[1], opcode[2]);  // AND_Gate
  ExactlyOne xor_1 (.out(ALUSrc), .in0(opcode[0]), .in1(opcode[1]), .in2(opcode[2]));
  and and_2 (MemWrite, ~opcode[0], opcode[1], ~opcode[2]);  // AND_Gate
  and and_3 (MemRead, opcode[0], ~opcode[1], ~opcode[2]);  // AND_Gate
  and and_4 (and_4_out, ~opcode[0], ~opcode[1], ~opcode[2]);  // AND_Gate
  and and_5 (and_5_out, ~opcode[0], ~opcode[1], opcode[2]);  // AND_Gate
  and and_6 (Branch, opcode[0], opcode[1], ~opcode[2]);  // AND_Gate
  and and_7 (Jump, opcode[0], opcode[1], opcode[2]);
  and and_8 (and_8_out, opcode[0], opcode[1], ~opcode[2]);  // AND_Gate
  and and_9 (and_9_out, ~opcode[0], ~opcode[1], opcode[2]);  // AND_Gate
  and and_10 (out_10[1], ~opcode[0], ~opcode[1]);  // AND_Gate
  or or_1 (RegWrite, nor_2_out, and_1_out);
  or or_2 (MemToReg, and_4_out, and_5_out);
  or or_3 (out_10[0], and_8_out, and_9_out);

  // Notes on the sheet:
  //   Unidade de controle
endmodule

module ULA (
  input  [7:0] A,
  input  [7:0] B,
  input  [2:0] \Função ,
  input  [2:0] Shamt,
  output [7:0] R,
  output Igual
);

  wire [7:0] AComp, adder_1_out, ADiv, AMult, ANeg, AShiftDir, AShiftEsq, ASoma, ASub, BComp, BDiv,
       bit_extender_1_out, BMult, BSoma, BSub, divider_1_out, multiplier_1_out, negator_1_out, shifter_1_out,
       shifter_2_out, subtractor_1_out;

  Demultiplexer #(.select(3), .width(8), .enable("false")) demultiplexer_1 (
    .out0(ASoma), .out1(ASub), .out2(AMult), .out3(ADiv), .out4(ANeg), .out5(AComp), .out6(AShiftEsq),
    .out7(AShiftDir), .in(A), .sel(\Função ));
  Demultiplexer #(.select(3), .width(8), .enable("false")) demultiplexer_2 (
    .out0(BSoma), .out1(BSub), .out2(BMult), .out3(BDiv), .out5(BComp), .in(B), .sel(\Função ));  // open: out4, out6, out7
  Adder adder_1 (.a(ASoma), .b(BSoma), .out(adder_1_out));  // open: cin, cout
  Subtractor subtractor_1 (.a(ASub), .b(BSub), .out(subtractor_1_out));  // open: bin, bout
  Multiplier multiplier_1 (.a(AMult), .b(BMult), .out(multiplier_1_out));  // open: cin, cout
  Divider divider_1 (.a(ADiv), .b(BDiv), .out(divider_1_out));  // open: upper, rem
  Negator negator_1 (.in(ANeg), .out(negator_1_out));
  Comparator comparator_1 (.a(AComp), .b(BComp), .eq(Igual));  // open: gt, lt
  Shifter shifter_1 (.in(AShiftEsq), .\dist (Shamt), .out(shifter_1_out));
  Shifter #(.shift("lr")) shifter_2 (.in(AShiftDir), .\dist (Shamt), .out(shifter_2_out));
  assign bit_extender_1_out = {{7{1'b0}}, Igual};  // Bit_Extender bit_extender_1
  Multiplexer #(.select(3), .width(8), .enable("false")) multiplexer_1 (
    .in0(adder_1_out), .in1(subtractor_1_out), .in2(multiplier_1_out), .in3(divider_1_out),
    .in4(negator_1_out), .in5(bit_extender_1_out), .in6(shifter_1_out), .in7(shifter_2_out), .out(R),
    .sel(\Função ));

  // Notes on the sheet:
  //   ULA
endmodule

module Banco_de_Registradores (
  input  [2:0] Read_register_1,
  input  [2:0] Read_register_2,
  input  [7:0] Write_data,
  input  [2:0] Write_register,
  input  RegWrite,
  input  CLOCK,
  input  CLEAR,
  output [7:0] Read_data_1,
  output [7:0] Read_data_2
);

  wire WE0, WE1, WE2, WE3, WE4, WE5, WE6, WE7;
  wire [7:0] demultiplexer_1_out0, demultiplexer_1_out1, demultiplexer_1_out2, demultiplexer_1_out3,
       demultiplexer_1_out4, demultiplexer_1_out5, demultiplexer_1_out6, demultiplexer_1_out7, Reg0, Reg1,
       Reg2, Reg3, Reg4, Reg5, Reg6, Reg7;

  Demultiplexer #(.select(3), .width(8), .enable("false")) demultiplexer_1 (
    .out0(demultiplexer_1_out0), .out1(demultiplexer_1_out1), .out2(demultiplexer_1_out2),
    .out3(demultiplexer_1_out3), .out4(demultiplexer_1_out4), .out5(demultiplexer_1_out5),
    .out6(demultiplexer_1_out6), .out7(demultiplexer_1_out7), .in(Write_data), .sel(Write_register));
  Demultiplexer #(.select(3), .enable("false")) demultiplexer_2 (
    .out0(WE0), .out1(WE1), .out2(WE2), .out3(WE3), .out4(WE4), .out5(WE5), .out6(WE6), .out7(WE7),
    .in(RegWrite), .sel(Write_register));
  Register u_Reg0 (.D(demultiplexer_1_out0), .en(WE0), .Q(Reg0), .clk(CLOCK), .clr(CLEAR));
  Register u_Reg1 (.D(demultiplexer_1_out1), .en(WE1), .Q(Reg1), .clk(CLOCK), .clr(CLEAR));
  Register u_Reg2 (.D(demultiplexer_1_out2), .en(WE2), .Q(Reg2), .clk(CLOCK), .clr(CLEAR));
  Register u_Reg3 (.D(demultiplexer_1_out3), .en(WE3), .Q(Reg3), .clk(CLOCK), .clr(CLEAR));
  Register u_Reg4 (.D(demultiplexer_1_out4), .en(WE4), .Q(Reg4), .clk(CLOCK), .clr(CLEAR));
  Register u_Reg5 (.D(demultiplexer_1_out5), .en(WE5), .Q(Reg5), .clk(CLOCK), .clr(CLEAR));
  Register u_Reg6 (.D(demultiplexer_1_out6), .en(WE6), .Q(Reg6), .clk(CLOCK), .clr(CLEAR));
  Register u_Reg7 (.D(demultiplexer_1_out7), .en(WE7), .Q(Reg7), .clk(CLOCK), .clr(CLEAR));
  Multiplexer #(.select(3), .width(8), .enable("false")) multiplexer_1 (
    .in0(Reg0), .in1(Reg1), .in2(Reg2), .in3(Reg3), .in4(Reg4), .in5(Reg5), .in6(Reg6), .in7(Reg7),
    .out(Read_data_1), .sel(Read_register_1));
  Multiplexer #(.select(3), .width(8), .enable("false")) multiplexer_2 (
    .in0(Reg0), .in1(Reg1), .in2(Reg2), .in3(Reg3), .in4(Reg4), .in5(Reg5), .in6(Reg6), .in7(Reg7),
    .out(Read_data_2), .sel(Read_register_2));

  // Other names for the same wires on the sheet: Read1[2:0] = Read_register_1; Read2[2:0] = Read_register_2

  // Notes on the sheet:
  //   Banco de Registradores
endmodule
